# Fritzing sketch IOT based Ecg and gps (saved by Fritzing 0.9.3b)

parts:
  U1 = LuaNode32 / ESP32 [part_number=ESP32S-PIN30]
  J1 = Piezo Speaker
  S1 = Round Pushbutton
  U2 = LIPO-1000mAh [package=lipo-1000]
  M1 = NEO-6M GPS Module [part_number=GY-GPS6MV2]
  M2 = TP4056 Module [part_number=HW-107]
  Mod1 = AD8232 HeartRate Monitor [part_number=SEN-12650]

nets:
  N1: U1.D33, Mod1.OUTPUT
  GND: U1.GND, J1.pin1, M1.GND, M2.OUT-#1, Mod1.GND
  N2: U1.Vin, S1.leg0
  3V3: U1.3V3, Mod1.3.3v
  N3: U1.RX2, M1.Tx
  N4: U1.TX2, M1.Rx
  N5: U1.D5, J1.pin2
  N6: S1.leg1, M2.OUT-#4
  N7: U2.+, M2.BAT+
  N8: U2.-, M2.BAT-

custom parts:
  LuaNode32 / ESP32: New Image for LuaNode32 DOIT ESP32 DEVKIT V1. Base parts from LuaNode32 / ESP32 ESP32 based LuaNode32 by G.Noorlander DOIT Esp32 DevKit v1 (30 pins long, 11 pins width) by Werner Rothschopf (modified by vanepp Dec 2018)
  NEO-6M GPS Module: GY-GPS6MV2 NEO-6M GPS Module Module based on U-blox NEO-6M GPS engine, incorporating regulator for 3.3-5V DC input, MS621FE-compatible rechargeable battery for backup and EEPROM for storing configuration settings. Links: NEO-6 series product information page NEO-6 Datasheet
  TP4056 Module: TP4056 Lithium Battery Charge Management Module Links: TP4056 website
  AD8232 HeartRate Monitor: Sparkfun single lead heart rate monitor - Ad8232.
